# Fritzing sketch bluetooth (saved by Fritzing 0.9.3b)
breadboards: 1

parts:
  Part1 = Arduino Uno (Rev3)
  Part2 = Bluetooth HC-06

nets:
  N1: Part1.D10_PWM/SS, Part2.RXD
  N2: Part1.D11_PWM/MOSI, Part2.TXD
  5V: Part1.5V, Part2.VCC
  GND: Part1.GND, Part2.GND
