# Fritzing sketch bluetooth-and-servo (saved by Fritzing 0.9.3b)
breadboards: 1

parts:
  Part1 = Arduino Uno (Rev3)
  Part2 = Bluetooth HC-06
  R1 = Resistor [tolerance=±5% resistance=20k package=THT]
  R2 = Resistor [tolerance=±5% resistance=10k package=THT]
  J1 = Basic Servo

nets:
  N1: Part1.D10_PWM/SS, J1.pulse
  N2: Part1.D2, R2.Pin_0
  N3: Part1.D4, Part2.TXD
  5V: Part1.5V, Part2.VCC
  GND: Part1.GND, Part2.GND, R1.Pin_1
  N4: Part2.RXD, R1.Pin_0, R2.Pin_1
