# Fritzing sketch wifi-servo-and-lights-2 (saved by Fritzing 0.9.3b)
breadboards: 1

parts:
  Part2 = Arduino MKR1000
  LED2 = LED - 5mm [color="Red (633nm)" package="5 mm [THT]"]
  J1 = Basic Servo
  LED5 = LED - 5mm [color="Yellow (595nm)" package="5 mm [THT]"]
  LED6 = LED - 5mm [color="White (4500K)" package="5 mm [THT]"]
  LED7 = LED - 5mm [color="Blue (525nm)" package="5 mm [THT]"]
  R8 = Resistor [tolerance=±5% resistance=10k package=THT]
  R9 = Resistor [tolerance=±5% resistance=10k package=THT]
  R10 = Resistor [tolerance=±5% resistance=10k package=THT]
  R11 = Resistor [tolerance=±5% resistance=10k package=THT]

nets:
  N1: Part2.A1, LED2.cathode
  N2: Part2.A2, LED5.cathode
  N3: Part2.A3, LED6.cathode
  N4: Part2.A4, LED7.cathode
  N5: Part2.D10_MISO, J1.pulse
  GND: Part2.GND, J1.gnd, R8.Pin_1, R9.Pin_1, R10.Pin_1, R11.Pin_1
  5V: Part2.5V, J1.vcc
  N6: LED2.anode, R8.Pin_0
  N7: LED5.anode, R9.Pin_0
  N8: LED6.anode, R10.Pin_0
  N9: LED7.anode, R11.Pin_0

custom parts:
  Arduino MKR1000: MKR1000 is a powerful board that combines the functionality of the Zero and the Wi-Fi Shield. It is the ideal solution for makers wanting to design IoT projects with minimal previous experience in networking
