# Fritzing sketch wifi-servo-and-lights (saved by Fritzing 0.9.3b)
breadboards: 1

parts:
  Part2 = Arduino MKR1000
  LED1 = LED - 5mm [color="Blue (505nm)" package="5 mm [THT]"]
  LED2 = LED - 5mm [color="Red (633nm)" package="5 mm [THT]"]
  J1 = Basic Servo

nets:
  N1: Part2.D8_MOSI, LED2.cathode
  N2: Part2.D10_MISO, J1.pulse
  GND: Part2.GND, LED1.cathode, LED2.anode, J1.gnd
  5V: Part2.5V, J1.vcc

custom parts:
  Arduino MKR1000: MKR1000 is a powerful board that combines the functionality of the Zero and the Wi-Fi Shield. It is the ideal solution for makers wanting to design IoT projects with minimal previous experience in networking
